# Fritzing sketch Arduino_Min_Sys_schematic (saved by Fritzing 0.9.4)
breadboards: 1

parts:
  IC3 = MICROCONTROLLER [package=dil28-3]
  R1 = Resistor [tolerance=±5% resistance=10k package="2512 [SMD]"]
  XTAL1 = Crystal [frequency="16 Mhz" package=SMD]
  22pF = Capacitor [package=cap-pth-small2]
  22pF_2 = Capacitor [package=cap-pth-small2]
  47uF = Capacitor Polarized [package=cpol-radial-10uf-25v]
  LED1 = LED - 3mm [color="Red (633nm)" package="3 mm [THT]"]
  R2 = Resistor [tolerance=±5% resistance=220 package="2512 [SMD]"]
  S1 = Pushbutton [package="[SMD]"]
  100nF = Capacitor [package=cap-pth-small2]

nets:
  N1: IC3.PC6(_RESET), R1.Pin_0, S1.Pin_1, S1.Pin_2, 100nF.2
  N2: IC3.VCC, IC3.AVCC, R1.Pin_1, 47uF.+
  N3: IC3.GND, IC3.AGND, 22pF.1, 22pF_2.2, 47uF.-, LED1.cathode, S1.Pin_3, S1.Pin_4
  N4: IC3.PB6(XTAL1_TOSC1), XTAL1.pin_0, 22pF.2
  N5: IC3.PB7(XTAL2_TOSC2), XTAL1.pin_1, 22pF_2.1
  N6: IC3.PB5(SCK), R2.Pin_1
  N7: LED1.anode, R2.Pin_0

notes:
  DTR
  RX
  TX
  VCC
  CTS
  GND
